# Fritzing sketch Tuan2 Sketch 3 (saved by Fritzing 0.9.5d)
breadboards: 1

parts:
  U1 = ESP32-38PinWide [part_number=ESP32-38PinWide]
  LED1 = smd LED [color="Red (633nm)" package="0805 [SMD]"]
  S1 = Pushbutton [package="[THT]"]
  S2 = Pushbutton [package="[THT]"]
  M1 = MAX7219 8x8 single Led Matrix Module
  LED2 = smd LED [color="Red (633nm)" package="0805 [SMD]"]

nets:
  N1: U1.GPIO32, LED2.anode
  N2: U1.GPIO25, S1.Pin_4
  N3: U1.GPIO26, U1.GPIO11, LED1.cathode, S1.Pin_1, S1.Pin_2, S2.Pin_3, S2.Pin_4, LED2.cathode
  N4: U1.GPIO27, LED1.anode
  N5: U1.VIN, M1.I-VCC, M1.O-VCC
  N6: U1.GPIO5, M1.I-CS, M1.O-CS
  N7: U1.GPIO18, M1.I-CLK, M1.O-CLK
  N8: U1.GPIO23, M1.I-DIN
  N9: U1.GND, M1.I-GND, M1.O-GND

custom parts:
  ESP32-38PinWide: Generic 38-Pin ESP32 with wide format (only access to one side of pins on a breadboard) based on Stephen Lilley's HiLetgo ESP-WROOM-32 ESP32 ESP-32S Development Board.
  MAX7219 8x8 single Led Matrix Module: Description: MAX7219 8x8 LedMatrix single Red Module Dimensions: 32x32mm Documents:
